# Fritzing sketch EduCaseComponentConnections (saved by Fritzing 0.9.3b)
breadboards: 1

parts:
  Raspberry_Pi_1 = Raspberry Pi 3 [part_number=RPI-3-V1.2]
  Battery_Supply = DC Power [voltage=12V]
  S1 = Taiway 100-SP-X-T1 SPDT Miniature Toggle Switch [part_number="Power Switch" package=THT]
  H1 = polarizedheader 4pin 0.156in [package=THT]  # not connected
  USB1 = Header 3 [part_number="Hub Supply" package=jst-3-smd]
  JP2 = Header 6 [package=1x06-smd]  # not connected
  CP1 = Header 2 [part_number=Charge package=jst-2-pth]
  PJ1 = mystery part, 3 pins [chip_label=Projector]  # not connected
  D1 = mystery part, 3 pins [chip_label="LCD Display"]
  CP2 = Header 2 [part_number=Port package=jst-2-pth]  # not connected
  CP3 = Header 2 [part_number="Power Control" package=jst-2-pth]
  U2 = mystery part, 3 pins [chip_label=" DC/DC Converter 5V"]
  RL1 = RELAY [part_number="Optional Power Control" package=relay-jzc]
  U3 = mystery part, 3 pins [chip_label=?]  # not connected
  P4 = Header 2 [part_number="Controller Supply" package=jst-2-pth]

nets:
  GND: Raspberry_Pi_1.GND, Battery_Supply.V-, USB1.2, CP1.2, D1.pin2, U2.pin1, P4.2
  N1: Raspberry_Pi_1.5V, USB1.3, U2.pin2, P4.1
  N2: Battery_Supply.V+, RL1.NC
  N3: S1.COM, D1.pin1, U2.pin3
  N4: S1.L2, RL1.MAIN
  N5: CP3.1, RL1.COIL2
  N6: CP3.2, RL1.COIL1

notes:
  Educase Portable Classroom, Educase Main Conn., 1.1
